// Digital circuit 4-bit-register-GPR.dig as structural Verilog
module _4_bit_register_GPR (
  input  clk,
  input  CLR,
  input  [3:0] Input,
  input  [1:0] Write,
  output [3:0] Output
);

  wire [3:0] multiplexer_1_out, not_1_out;

  assign not_1_out = ~4'b0000;  // Not not_1, 4 bits wide
  Multiplexer #(.Selector_Bits(2), .Bits(4)) multiplexer_1 (
    .sel(Write), .in_0(Output), .in_1(Input), .in_2(4'b0000), .in_3(not_1_out), .out(multiplexer_1_out));
  D_FF_AS d_ff_as_1 (.Set(1'b0), .D(multiplexer_1_out[3]), .C(clk), .Clr(CLR), .Q(Output[3]));  // open: nQ
  D_FF_AS d_ff_as_2 (.Set(1'b0), .D(multiplexer_1_out[2]), .C(clk), .Clr(CLR), .Q(Output[2]));  // open: nQ
  D_FF_AS d_ff_as_3 (.Set(1'b0), .D(multiplexer_1_out[1]), .C(clk), .Clr(CLR), .Q(Output[1]));  // open: nQ
  D_FF_AS d_ff_as_4 (.Set(1'b0), .D(multiplexer_1_out[0]), .C(clk), .Clr(CLR), .Q(Output[0]));  // open: nQ
endmodule
