// Digital circuit 4x1 Multiplexer + En.dig as structural Verilog
module _4x1_Multiplexer___En (
  input  S0,
  input  S1,
  input  I_0,
  input  I_1,
  input  I_2,
  input  I_3,
  input  E,
  output Output
);

  wire and_1_out, and_2_out, and_3_out, and_4_out, not_1_out, not_2_out, or_1_out;

  not not_1 (not_1_out, S0);
  not not_2 (not_2_out, S1);
  and and_1 (and_1_out, not_1_out, not_2_out, I_0);
  and and_2 (and_2_out, not_1_out, S1, I_1);
  and and_3 (and_3_out, S0, not_2_out, I_2);
  and and_4 (and_4_out, S0, S1, I_3);
  or or_1 (or_1_out, and_1_out, and_2_out, and_3_out, and_4_out);
  and and_5 (Output, or_1_out, E);
endmodule
