// Digital circuit GPR_Register_1.dig as structural Verilog
module GPR_Register_1 (
  input  clk,
  input  CLR,
  input  ST,
  input  S0,
  input  S1,
  input  [3:0] I_0,
  input  [3:0] I_1,
  input  [3:0] I_2,
  input  [3:0] I_3,
  input  [1:0] LD,
  output [3:0] Output
);

  wire [3:0] R0_output, R1_output, R2_output, R3_output;

  _4_bit_register_GPR R0 (.clk(clk), .CLR(CLR), .Input(I_0), .Write(LD), .Output(R0_output));
  _4_bit_register_GPR R1 (.clk(clk), .CLR(CLR), .Input(I_1), .Write(LD), .Output(R1_output));
  _4_bit_register_GPR R2 (.clk(clk), .CLR(CLR), .Input(I_2), .Write(LD), .Output(R2_output));
  _4_bit_register_GPR R3 (.clk(clk), .CLR(CLR), .Input(I_3), .Write(LD), .Output(R3_output));
  _4x1_Multiplexer_4bit _4x1_multiplexer_4bit_1 (
    .I_0(R0_output), .I_1(R1_output), .I_2(R2_output), .I_3(R3_output), .S0(S0), .S1(S1), .E(ST),
    .Output(Output));
endmodule
