// Digital circuit GPR_Register.dig as structural Verilog
module GPR_Register (
  input  [3:0] BUS_IN,
  input  [3:0] IMM,
  input  [3:0] ALU_OUT,
  input  [1:0] LD_R0,
  input  [1:0] LD_R1,
  input  [1:0] LD_R2,
  input  [1:0] LD_R3,
  input  clk,
  input  CLR,
  input  ST,
  input  [3:0] BUS_IN_2,
  input  [3:0] IMM_2,
  input  [3:0] ALU_OUT_2,
  input  [3:0] BUS_IN_3,
  input  [3:0] IMM_3,
  input  [3:0] ALU_OUT_3,
  input  [3:0] BUS_IN_4,
  input  [3:0] IMM_4,
  input  [3:0] ALU_OUT_4,
  input  [1:0] Sel_0,
  input  S0,
  input  S1,
  output [3:0] Output
);

  wire [3:0] multiplexer_1_out, multiplexer_2_out, multiplexer_3_out, multiplexer_4_out, R0_output,
       R1_output, R2_output, R3_output;

  Multiplexer #(.Bits(4), .Selector_Bits(2)) multiplexer_1 (
    .sel(Sel_0), .in_0(BUS_IN), .in_1(IMM), .in_2(ALU_OUT), .in_3(4'b0000), .out(multiplexer_1_out));
  Multiplexer #(.Bits(4), .Selector_Bits(2)) multiplexer_2 (
    .sel(Sel_0), .in_0(BUS_IN_2), .in_1(IMM_2), .in_2(ALU_OUT_2), .in_3(4'b0000), .out(multiplexer_2_out));
  Multiplexer #(.Bits(4), .Selector_Bits(2)) multiplexer_3 (
    .sel(Sel_0), .in_0(BUS_IN_3), .in_1(IMM_3), .in_2(ALU_OUT_3), .in_3(4'b0000), .out(multiplexer_3_out));
  Multiplexer #(.Bits(4), .Selector_Bits(2)) multiplexer_4 (
    .sel(Sel_0), .in_0(BUS_IN_4), .in_1(IMM_4), .in_2(ALU_OUT_4), .in_3(4'b0000), .out(multiplexer_4_out));
  _4_bit_register_GPR R0 (.clk(clk), .CLR(CLR), .Input(multiplexer_1_out), .Write(LD_R0), .Output(R0_output));
  _4_bit_register_GPR R1 (.clk(clk), .CLR(CLR), .Input(multiplexer_2_out), .Write(LD_R1), .Output(R1_output));
  _4_bit_register_GPR R2 (.clk(clk), .CLR(CLR), .Input(multiplexer_3_out), .Write(LD_R2), .Output(R2_output));
  _4_bit_register_GPR R3 (.clk(clk), .CLR(CLR), .Input(multiplexer_4_out), .Write(LD_R3), .Output(R3_output));
  _4x1_Multiplexer_4bit _4x1_multiplexer_4bit_1 (
    .I_0(R0_output), .I_1(R1_output), .I_2(R2_output), .I_3(R3_output), .S0(S0), .S1(S1), .E(ST),
    .Output(Output));
endmodule
