// Digital circuit 4-bit-ProgramCounter.dig as structural Verilog
module _4_bit_ProgramCounter (
  input  LD,
  input  INC,
  input  [3:0] JumpAddr_1,
  input  [3:0] JumpAddr_2,
  input  clk,
  input  RST,
  output [3:0] PC
);

  wire [3:0] _4_bit_adder_1_sum, _4x1_multiplexer_4bit_1_output;

  _4_bit_adder _4_bit_adder_1 (.A(PC), .B(4'b0001), .Sum(_4_bit_adder_1_sum));  // open: Overflow_flag
  _4x1_Multiplexer_4bit _4x1_multiplexer_4bit_1 (
    .S0(LD), .S1(INC), .I_0(PC), .I_1(_4_bit_adder_1_sum), .I_2(JumpAddr_1), .I_3(JumpAddr_2),
    .Output(_4x1_multiplexer_4bit_1_output));
  _4_bit_register_GPR PC_Register (
    .clk(clk), .CLR(RST), .Input(_4x1_multiplexer_4bit_1_output), .Write(2'b01), .Output(PC));
endmodule
