// Digital circuit 4x1-Multiplexer-4bit.dig as structural Verilog
module _4x1_Multiplexer_4bit (
  input  S0,
  input  S1,
  input  [3:0] I_0,
  input  [3:0] I_1,
  input  [3:0] I_2,
  input  [3:0] I_3,
  output [3:0] Output
);

  _4x1_Multiplexer _4x1_multiplexer_1 (
    .S0(S0), .S1(S1), .I_0(I_0[0]), .I_1(I_1[0]), .I_2(I_2[0]), .I_3(I_3[0]), .Output(Output[0]));
  _4x1_Multiplexer _4x1_multiplexer_2 (
    .S0(S0), .S1(S1), .I_0(I_0[1]), .I_1(I_1[1]), .I_2(I_2[1]), .I_3(I_3[1]), .Output(Output[1]));
  _4x1_Multiplexer _4x1_multiplexer_3 (
    .S0(S0), .S1(S1), .I_0(I_0[2]), .I_1(I_1[2]), .I_2(I_2[2]), .I_3(I_3[2]), .Output(Output[2]));
  _4x1_Multiplexer _4x1_multiplexer_4 (
    .S0(S0), .S1(S1), .I_0(I_0[3]), .I_1(I_1[3]), .I_2(I_2[3]), .I_3(I_3[3]), .Output(Output[3]));
endmodule
