// Digital circuit Registers_DRAM.dig as structural Verilog
module Registers_DRAM (
  input  CS,
  input  WE,
  input  OE,
  input  LD,
  input  INC,
  input  [3:0] JumpAddr_1,
  input  [3:0] JumpAddr_2,
  input  RST,
  input  clk,
  input  clk_2,
  input  [1:0] LD_2,
  input  S,
  input  [1:0] LD_R0,
  input  [1:0] LD_R1,
  input  [1:0] LD_R2,
  input  [1:0] LD_R3,
  input  clk_3,
  input  CLR,
  input  ST,
  input  S0,
  input  S1,
  input  [3:0] I_0,
  input  [3:0] I_1,
  input  [3:0] I_2,
  input  [3:0] I_3,
  input  E,
  input  [3:0] IN,
  output [3:0] Output
);

  wire [3:0] _4_bit_programcounter_1_pc, _4x1_multiplexer_4bit_1_output, IR_output, Memory_d, R0_output,
       R1_output, R2_output, R3_output;

  _4_bit_ProgramCounter _4_bit_programcounter_1 (
    .LD(LD), .INC(INC), .JumpAddr_1(JumpAddr_1), .JumpAddr_2(JumpAddr_2), .clk(clk), .RST(RST),
    .PC(_4_bit_programcounter_1_pc));
  RAMSinglePortSel #(.AddrBits(4), .Bits(4)) Memory (
    .A(_4_bit_programcounter_1_pc), .CS(CS), .WE(WE), .OE(OE), .D(Memory_d));
  _4_bit_register_GPR R0 (.clk(clk_3), .CLR(CLR), .Input(I_0), .Write(LD_R0), .Output(R0_output));
  _4_bit_register_GPR R1 (.clk(clk_3), .CLR(CLR), .Input(I_1), .Write(LD_R1), .Output(R1_output));
  _4_bit_register_GPR R2 (.clk(clk_3), .CLR(CLR), .Input(I_2), .Write(LD_R2), .Output(R2_output));
  _4_bit_register_GPR R3 (.clk(clk_3), .CLR(CLR), .Input(I_3), .Write(LD_R3), .Output(R3_output));
  _4_bit_Register IR (.clk(clk_2), .Input(IN), .Write(LD_2), .\output (IR_output));
  _4x1_Multiplexer_4bit _4x1_multiplexer_4bit_1 (
    .I_0(R0_output), .I_1(R1_output), .I_2(R2_output), .I_3(R3_output), .S0(S0), .S1(S1), .E(ST),
    .Output(_4x1_multiplexer_4bit_1_output));
  Multiplexer #(.Bits(4)) multiplexer_1 (
    .sel(S), .in_0(IR_output), .in_1(_4x1_multiplexer_4bit_1_output), .out(Memory_d));
  assign Output = E ? Memory_d : 4'bz;  // Driver driver_1
endmodule
