// Digital circuit Registers_DRAM_1.dig as structural Verilog
module Registers_DRAM_1 (
  input  CS,
  input  WE,
  input  OE,
  input  LD,
  input  INC,
  input  [3:0] JumpAddr_1,
  input  [3:0] JumpAddr_2,
  input  RST,
  input  clk,
  input  clk_2,
  input  [1:0] LD_2,
  input  [3:0] BUS_IN,
  input  [3:0] IMM,
  input  [3:0] ALU_OUT,
  input  [1:0] LD_R0,
  input  [1:0] LD_R1,
  input  [1:0] LD_R2,
  input  [1:0] LD_R3,
  input  clk_3,
  input  CLR,
  input  ST,
  input  [3:0] BUS_IN_2,
  input  [3:0] IMM_2,
  input  [3:0] ALU_OUT_2,
  input  [3:0] BUS_IN_3,
  input  [3:0] IMM_3,
  input  [3:0] ALU_OUT_3,
  input  [3:0] BUS_IN_4,
  input  [3:0] IMM_4,
  input  [3:0] ALU_OUT_4,
  input  [1:0] Sel_0,
  input  S0,
  input  S1,
  input  RAM_OUT_EN,
  input  GPR_OUT_EN,
  output [3:0] Output,
  output [3:0] Output_2
);

  wire [3:0] _4_bit_programcounter_1_pc, driver_1_out, Memory_d, multiplexer_1_out, multiplexer_2_out,
       multiplexer_3_out, multiplexer_4_out, R0_output, R1_output, R2_output, R3_output;

  _4_bit_ProgramCounter _4_bit_programcounter_1 (
    .LD(LD), .INC(INC), .JumpAddr_1(JumpAddr_1), .JumpAddr_2(JumpAddr_2), .clk(clk), .RST(RST),
    .PC(_4_bit_programcounter_1_pc));
  RAMSinglePortSel #(.AddrBits(4), .Bits(4)) Memory (
    .A(_4_bit_programcounter_1_pc), .CS(CS), .WE(WE), .OE(OE), .D(Memory_d));
  assign driver_1_out = RAM_OUT_EN ? Memory_d : 4'bz;  // Driver driver_1
  _4_bit_Register IR (.clk(clk_2), .Input(driver_1_out), .Write(LD_2), .\output (Output));
  Multiplexer #(.Selector_Bits(2), .Bits(4)) multiplexer_1 (
    .sel(Sel_0), .in_0(BUS_IN), .in_1(IMM), .in_2(ALU_OUT), .in_3(driver_1_out), .out(multiplexer_1_out));
  Multiplexer #(.Selector_Bits(2), .Bits(4)) multiplexer_2 (
    .sel(Sel_0), .in_0(BUS_IN_2), .in_1(IMM_2), .in_2(ALU_OUT_2), .in_3(driver_1_out), .out(multiplexer_2_out));
  Multiplexer #(.Selector_Bits(2), .Bits(4)) multiplexer_3 (
    .sel(Sel_0), .in_0(BUS_IN_3), .in_1(IMM_3), .in_2(ALU_OUT_3), .in_3(driver_1_out), .out(multiplexer_3_out));
  Multiplexer #(.Selector_Bits(2), .Bits(4)) multiplexer_4 (
    .sel(Sel_0), .in_0(BUS_IN_4), .in_1(IMM_4), .in_2(ALU_OUT_4), .in_3(driver_1_out), .out(multiplexer_4_out));
  _4_bit_register_GPR R0 (.clk(clk_3), .CLR(CLR), .Input(multiplexer_1_out), .Write(LD_R0), .Output(R0_output));
  _4_bit_register_GPR R1 (.clk(clk_3), .CLR(CLR), .Input(multiplexer_2_out), .Write(LD_R1), .Output(R1_output));
  _4_bit_register_GPR R2 (.clk(clk_3), .CLR(CLR), .Input(multiplexer_3_out), .Write(LD_R2), .Output(R2_output));
  _4_bit_register_GPR R3 (.clk(clk_3), .CLR(CLR), .Input(multiplexer_4_out), .Write(LD_R3), .Output(R3_output));
  _4x1_Multiplexer_4bit _4x1_multiplexer_4bit_1 (
    .I_0(R0_output), .I_1(R1_output), .I_2(R2_output), .I_3(R3_output), .S0(S0), .S1(S1), .E(ST),
    .Output(Output_2));
  assign Output_2 = GPR_OUT_EN ? driver_1_out : 4'bz;  // Driver driver_2
endmodule
